# Fritzing sketch LED (saved by Fritzing 0.9.3b)
breadboards: 1

parts:
  Part1 = Arduino Uno (Rev3)
  LED1 = smd LED [color="Red (633nm)" package="0603 [SMD]"]
  R1 = Resistor [tolerance=±5% resistance=220 package=THT]

nets:
  N1: Part1.GND, LED1.cathode
  N2: Part1.5V, R1.Pin_1
  N3: LED1.anode, R1.Pin_0

// code stored in the sketch: LEDcode.ino
#include <Servo.h>

Servo motor;
int pos = 0;

void setup() {
pinMode(11,INPUT_PULLUP);
Serial.begin(9600);
motor.attach(9);
}

void loop() 
{
  if (digitalRead(11) == LOW)
  {
    Serial.print("WORKS");
    for (pos = 0; pos < 180; pos += 40)
    {
    motor.write(pos);
    delay(15);
    }
    motor.write(175);
    delay(3000);
    for (pos = 180; pos > 0; pos -= 20)
    {
      motor.write(pos);
      delay(15);
    }
    motor.write(5);
  }
}
